// Logisim project Siln8 zad_1.circ as structural Verilog
module main (
  input  A,
  input  B,
  input  C,
  input  D,
  output Y_ZAD,
  output Z_ZAD,
  output Y_DNF,
  output Z_DNF,
  output Y_KNF,
  output Z_KNF
);

  wire A_B_out, B_C_D_out, n_B_D_out, n_C_nD_out, nA_nB_out, nB_C_out, nB_nC_D_out, nB_nD_C_out, nC_B_out,
       nD_C_nA_out, not_1_out, not_2_out, not_3_out, not_4_out, not_5_out, not_6_out, not_7_out, not_8_out,
       not_9_out, not_10_out, not_11_out, not_12_out;

  not not_1 (not_1_out, D);
  or A_B (A_B_out, A, B);
  nor n_C_nD (n_C_nD_out, C, not_1_out);
  nand n_B_D (n_B_D_out, B, D);
  not not_2 (not_2_out, A);
  not not_3 (not_3_out, B);
  not not_4 (not_4_out, B);
  not not_5 (not_5_out, C);
  not not_6 (not_6_out, B);
  not not_7 (not_7_out, D);
  not not_8 (not_8_out, A);
  not not_9 (not_9_out, D);
  not not_10 (not_10_out, C);
  not not_11 (not_11_out, B);
  nand n__A_B__n_C_nD (Y_ZAD, A_B_out, n_C_nD_out);
  xnor n_n_C_nD__n_D_B (Z_ZAD, n_C_nD_out, n_B_D_out);
  and nA_nB (nA_nB_out, not_2_out, not_3_out);
  not not_12 (not_12_out, D);
  and nB_nC_D (nB_nC_D_out, not_4_out, not_5_out, D);
  and B_C_D (B_C_D_out, B, C, D);
  or nB_nD_C (nB_nD_C_out, not_6_out, C, not_7_out);
  or nD_C_nA (nD_C_nA_out, not_8_out, C, not_9_out);
  or nC_B (nC_B_out, B, not_10_out);
  or nB_C (nB_C_out, not_11_out, C);
  or nA_nB__nD_C (Y_DNF, nA_nB_out, not_12_out, C);
  or C_B_D___nC_D_nB (Z_DNF, nB_nC_D_out, B_C_D_out);
  and nD_C_nA___nB_nD_C (Y_KNF, nB_nD_C_out, nD_C_nA_out);
  and C_nB___nC_B__D (Z_KNF, D, nC_B_out, nB_C_out);
endmodule

module DNF (
  input  A,
  input  B,
  input  C,
  input  D,
  output Y_ZAD,
  output Z_ZAD
);

  wire and_1_out, and_2_out, and_3_out, not_1_out, not_2_out, not_3_out, not_4_out, not_5_out;

  not not_1 (not_1_out, A);
  and and_1 (and_1_out, not_1_out, not_2_out);
  not not_2 (not_2_out, B);
  not not_3 (not_3_out, D);
  not not_4 (not_4_out, B);
  not not_5 (not_5_out, C);
  and and_2 (and_2_out, not_4_out, not_5_out, D);
  and and_3 (and_3_out, B, C, D);
  or or_1 (Y_ZAD, and_1_out, not_3_out, C);
  or or_2 (Z_ZAD, and_2_out, and_3_out);
endmodule

module KNF (
  input  A,
  input  B,
  input  C,
  input  D,
  output Y_ZAD,
  output Z_ZAD
);

  wire not_1_out, not_2_out, not_3_out, not_4_out, not_5_out, not_6_out, or_1_out, or_2_out, or_3_out,
       or_4_out;

  not not_1 (not_1_out, B);
  or or_1 (or_1_out, not_1_out, C, not_2_out);
  not not_2 (not_2_out, D);
  not not_3 (not_3_out, A);
  or or_2 (or_2_out, not_3_out, C, not_4_out);
  not not_4 (not_4_out, D);
  or or_3 (or_3_out, B, not_5_out);
  not not_5 (not_5_out, C);
  not not_6 (not_6_out, B);
  or or_4 (or_4_out, not_6_out, C);
  and and_1 (Y_ZAD, or_1_out, or_2_out);
  and and_2 (Z_ZAD, D, or_3_out, or_4_out);
endmodule
