// Logisim project 2_zad.circ as structural Verilog: 1 circuit, main circuit main
module main (
  input  a,
  input  b,
  input  c,
  input  d,
  output A_K,
  output B_K,
  output C_K,
  output D_K,
  output E_K,
  output A_D,
  output B_D,
  output C_D,
  output D_D,
  output E_D
);

  wire n_a_b_out, n_a_nb_out, n_b_c_d_out, n_b_c_out, n_b_d_out, n_b_nc_nd_out, n_b_nc_out, n_b_nd_out,
       n_d_na_out, n_nb_c_d_out, n_nb_c_out, n_nb_d_out, n_nb_na_nd_out, n_nb_nc_nd_out, n_nb_nc_out,
       n_nb_nd_out, na_2_out, na_out, nb_2_out, nb_out, nc_2_out, nc_out, nd_2_out, nd_out;

  nand na (na_out, a, a);
  not na_2 (na_2_out, a);  // NOR_Gate
  nand nc (nc_out, c, c);
  nand nb (nb_out, b, b);
  not nc_2 (nc_2_out, c);  // NOR_Gate
  not nb_2 (nb_2_out, b);  // NOR_Gate
  nand nd (nd_out, d, d);
  not nd_2 (nd_2_out, d);  // NOR_Gate
  nand n_a_nb (n_a_nb_out, a, nb_out);
  nand n_b_nc_nd (n_b_nc_nd_out, b, nc_out, nd_out);
  nand n_b_nc (n_b_nc_out, b, nc_out);
  nand n_nb_d (n_nb_d_out, nb_out, d);
  nand n_nb_c (n_nb_c_out, nb_out, c);
  nand n_b_nd (n_b_nd_out, b, nd_out);
  nand n_nb_c_d (n_nb_c_d_out, nb_out, d, c);
  nand n_d_na (n_d_na_out, na_out, d, d);
  nand n__a_nb__n_b_nc_nd (B_D, n_a_nb_out, n_b_nc_nd_out);
  nand n_n_b_nc__n_nb_d__n_nb_c (C_D, n_b_nc_out, n_nb_d_out, n_nb_c_out);
  nand n_n_b_nc__n_b_nd__n_nb_c (D_D, n_b_nc_out, n_nb_c_out, n_b_nd_out);
  nand n_n_d_na__n_d_na__n_b_nd (E_D, n_nb_c_d_out, n_d_na_out, n_b_nd_out);
  nor n_nb_nc (n_nb_nc_out, nb_2_out, nc_2_out);
  nor n_nb_nd (n_nb_nd_out, nb_2_out, nd_2_out);
  nor n_a_b (n_a_b_out, a, b);
  nor n_b_c_d (n_b_c_d_out, b, c, d);
  nor n_b_c (n_b_c_out, c, b);
  nor n_nb_nc_nd (n_nb_nc_nd_out, nb_2_out, nc_2_out, nd_2_out);
  nor n_nb_na_nd (n_nb_na_nd_out, nb_2_out, na_2_out, nd_2_out);
  nor n_b_d (n_b_d_out, b, d);
  nor n_n_nb_nc__n_nb_nd__n_a_b (B_K, n_nb_nc_out, n_a_b_out, n_nb_nd_out);
  nor n_n_b_c_d__n_nb_nc (C_K, n_nb_nc_out, n_b_c_d_out);
  nor n_n_b_c__n_nb_nc_nd (D_K, n_nb_nc_nd_out, n_b_c_out);
  nor n_n_nb_na_nd__n_b_d__n_b_c (E_K, n_b_c_out, n_nb_na_nd_out, n_b_d_out);

  assign A_D = a;
  assign A_K = a;
endmodule
