// Logisim project 3_zad.circ as structural Verilog: 1 circuit, main circuit main
module main (
  input  X,
  input  Res,
  output Y
);

  wire CLK_out, j_k_ff_1_q, j_k_ff_1_qn, j_k_ff_2_q, j_k_ff_2_qn, j_k_ff_3_q, j_k_ff_3_qn, nand_1_out,
       nand_3_out, nand_4_out, nand_5_out, nand_6_out, nand_7_out, nX_nZ1_nZ2_Z3_out, nX_Z2_Z3_out,
       nZ2_X_out, X_Z2_nZ3_out, Z1_nX_out, Z1_nZ3_out, Z1_X_out, Z1_Z2_X_out;

  nand nand_1 (nand_1_out, X, X);
  Clock CLK (.out(CLK_out));
  nand X_Z2_nZ3 (X_Z2_nZ3_out, X, j_k_ff_2_q, j_k_ff_3_qn);
  nand nX_Z2_Z3 (nX_Z2_Z3_out, nand_1_out, j_k_ff_2_q, j_k_ff_3_q);
  nand Z1_nZ3 (Z1_nZ3_out, j_k_ff_1_q, j_k_ff_3_qn);
  nand Z1_Z2_X (Z1_Z2_X_out, j_k_ff_1_q, j_k_ff_2_q, X);
  nand Z1_nX (Z1_nX_out, j_k_ff_1_q, nand_1_out);
  nand Z1_X (Z1_X_out, X, j_k_ff_1_q);
  nand nX_nZ1_nZ2_Z3 (nX_nZ1_nZ2_Z3_out, j_k_ff_1_qn, j_k_ff_3_q, j_k_ff_2_qn, nand_1_out);
  nand nZ2_X (nZ2_X_out, X, j_k_ff_2_qn);
  not nand_2 (Y, Z1_Z2_X_out);  // NAND_Gate
  nand nand_3 (nand_3_out, nZ2_X_out, nZ2_X_out);
  nand nand_4 (nand_4_out, X_Z2_nZ3_out, nX_Z2_Z3_out);
  nand nand_5 (nand_5_out, Z1_nZ3_out, Z1_Z2_X_out, Z1_nX_out);
  nand nand_6 (nand_6_out, Z1_X_out, nX_nZ1_nZ2_Z3_out, Z1_nZ3_out);
  nand nand_7 (nand_7_out, Z1_nX_out, nX_nZ1_nZ2_Z3_out);
  J_K_Flip_Flop j_k_ff_1 (
    .J(nand_4_out), .clk(CLK_out), .K(nand_5_out), .Q(j_k_ff_1_q), .Qn(j_k_ff_1_qn), .reset(Res));  // open: preset, en
  J_K_Flip_Flop j_k_ff_2 (
    .J(nand_6_out), .clk(CLK_out), .K(j_k_ff_1_qn), .Q(j_k_ff_2_q), .Qn(j_k_ff_2_qn), .reset(Res));  // open: preset, en
  J_K_Flip_Flop j_k_ff_3 (
    .J(nand_3_out), .clk(CLK_out), .K(nand_7_out), .Q(j_k_ff_3_q), .Qn(j_k_ff_3_qn), .reset(Res));  // open: preset, en
endmodule
