// Logisim project 1_zad.circ as structural Verilog: 1 circuit, main circuit main
module main (
  input  A,
  input  B,
  input  C,
  input  D,
  output Y_zad,
  output Z_zad
);

  wire nand_1_out, not_1_out, or_1_out, xnor_1_out;

  not not_1 (not_1_out, D);
  xnor xnor_1 (xnor_1_out, A, B);
  nand nand_1 (nand_1_out, C, not_1_out);
  or or_1 (or_1_out, B, D);
  xor xor_1 (Y_zad, xnor_1_out, nand_1_out);
  nor nor_1 (Z_zad, nand_1_out, or_1_out);
endmodule
