// Logisim project Matuška_zadanie1PPI.circ as structural Verilog: 1 circuit, main circuit main
module main (
  input  A,
  input  B,
  input  C,
  input  D,
  output Y_zad,
  output Z_zad,
  output Y_DNF,
  output Z_DNF,
  output Y_KNF,
  output Z_KNF
);

  wire A__nB_C_nD_out, A_B_D_out, A_B_nC_out, B_D_2_out, B_D_out, B_nC___B_D_out, B_nC_out, n_A_B_out,
       n_C_nD_out, nB_C_nD_out, not_1_out, not_2_out, not_3_out, not_4_out, not_5_out, not_6_out, not_7_out,
       not_8_out, not_9_out;

  not not_1 (not_1_out, B);
  not not_2 (not_2_out, D);
  not not_3 (not_3_out, C);
  not not_4 (not_4_out, B);
  not not_5 (not_5_out, D);
  not not_6 (not_6_out, C);
  not not_7 (not_7_out, B);
  not not_8 (not_8_out, D);
  not not_9 (not_9_out, D);
  and nB_C_nD (nB_C_nD_out, not_1_out, C, not_2_out);
  and B_nC (B_nC_out, B, not_3_out);
  and B_D (B_D_out, B, D);
  and A_B_nC (A_B_nC_out, A, B, not_6_out);
  and A_B_D (A_B_D_out, A, B, D);
  xnor n_A_B (n_A_B_out, A, B);
  nand n_C_nD (n_C_nD_out, C, not_9_out);
  or B_D_2 (B_D_2_out, B, D);
  or A__nB_C_nD (A__nB_C_nD_out, A, nB_C_nD_out);
  or B_nC___B_D (B_nC___B_D_out, B_nC_out, B_D_out);
  and nB_C_nD_2 (Z_DNF, not_4_out, C, not_5_out);
  or A_B_nC_A_B_D (Y_KNF, A_B_nC_out, A_B_D_out);
  and nB_C_nD_3 (Z_KNF, not_7_out, C, not_8_out);
  xor n_A_B__n_C_nD (Y_zad, n_A_B_out, n_C_nD_out);
  nor n_n_C_nD___B_D (Z_zad, n_C_nD_out, B_D_2_out);
  or A_nB_C_nD___B_nC_B_D (Y_DNF, A__nB_C_nD_out, B_nC___B_D_out);
endmodule
