// Logisim project main_zad2.circ as structural Verilog: 1 circuit, main circuit main
module main (
  input  a,
  input  b,
  input  c,
  input  d,
  output A_D,
  output B_D,
  output C_D,
  output D_D,
  output out_9,
  output out_10,
  output out_11,
  output out_12
);

  wire n_a_b_out, n_a_c_d_out, n_b_c_d_out, n_b_c_out, n_b_d_out, n_b_nc_nd_out, n_c_d_out, n_c_nd_out,
       n_nb_c_nd_out, n_nb_d_2_out, n_nb_d_out, n_nb_nc_out, n_nc_d_out, n_nc_nd_out, na_2_out, na_out,
       nb_2_out, nb_out, nc_2_out, nc_out, nd_2_out, nd_out;

  nand na (na_out, a, a);
  nor na_2 (na_2_out, a, a);
  nand nb (nb_out, b, b);
  nor nb_2 (nb_2_out, b, b);
  nand nc (nc_out, c, c);
  nor nc_2 (nc_2_out, c, c);
  nand nd (nd_out, d, d);
  nor nd_2 (nd_2_out, d, d);
  nand n_b_c (n_b_c_out, b, c);
  nand n_b_d (n_b_d_out, b, d);
  nand n_b_nc_nd (n_b_nc_nd_out, b, nc_out, nd_out);
  nand n_nb_c_nd (n_nb_c_nd_out, nb_out, c, nd_out);
  nand n_nb_d (n_nb_d_out, nb_out, d);
  nand n_c_nd (n_c_nd_out, c, nd_out);
  nand n_nc_d (n_nc_d_out, nc_out, d);
  nor n_a_c_d (n_a_c_d_out, a, c, d);
  nor n_a_b (n_a_b_out, a, b);
  nor n_nb_d_2 (n_nb_d_2_out, nb_2_out, d);
  nor n_nb_nc (n_nb_nc_out, nb_2_out, nc_2_out);
  nor n_b_c_d (n_b_c_d_out, b, c, d);
  nor n_c_d (n_c_d_out, c, d);
  nor n_nc_nd (n_nc_nd_out, nc_2_out, nd_2_out);
  nand n_n_b_c__na_n_b_d (A_D, n_b_c_out, na_out, n_b_d_out);
  nand n_n_b_nc_nd__n_nb_c_nd__n_nb_d (B_D, n_b_nc_nd_out, n_nb_c_nd_out, n_nb_d_out);
  nand n_n_c_nd__n_nc_d (C_D, n_c_nd_out, n_nc_d_out);
  nor n_n_a_c_d__n_a_b (out_9, n_a_c_d_out, n_a_b_out);
  nor n_n_nb_d__n_nb_nc__n_b_c_d (out_10, n_nb_d_2_out, n_nb_nc_out, n_b_c_d_out);
  nor n_n_c_d__n_nc_nd (out_11, n_c_d_out, n_nc_nd_out);

  assign D_D = d;
  assign out_12 = d;
endmodule
