// Logisim project 3_zad.circ as structural Verilog: 1 circuit, main circuit main
module main (
  input  X,
  input  Res,
  output Y
);

  wire CLK_out, J1_out, J2_out, J3_out, j_k_ff_1_q, j_k_ff_1_qn, j_k_ff_2_q, j_k_ff_2_qn, j_k_ff_3_q,
       j_k_ff_3_qn, K1_out, K3_out, nand_1_out, nZ1_nX_out, Z1_nX_out, Z1_Z2_X_out, Z2_nX_nZ3_out, Z2_nX_out,
       Z2_Z3_X_out, Z3_nX_out;

  nand nand_1 (nand_1_out, X, X);
  Clock CLK (.out(CLK_out));
  nand Z2_nX_nZ3 (Z2_nX_nZ3_out, nand_1_out, j_k_ff_2_q, j_k_ff_3_qn);
  nand Z2_Z3_X (Z2_Z3_X_out, X, j_k_ff_2_q, j_k_ff_3_q);
  nand Z1_nX (Z1_nX_out, X, j_k_ff_1_q);
  nand nZ1_nX (nZ1_nX_out, j_k_ff_1_qn, nand_1_out);
  nand Z2_nX (Z2_nX_out, nand_1_out, j_k_ff_2_q);
  nand Z3_nX (Z3_nX_out, nand_1_out, j_k_ff_3_q);
  nand Z1_Z2_X (Z1_Z2_X_out, j_k_ff_1_q, X, j_k_ff_2_q);
  nand J1 (J1_out, Z2_nX_nZ3_out, Z2_Z3_X_out);
  nand K1 (K1_out, X, j_k_ff_3_qn);
  not J3 (J3_out, Z1_nX_out);  // NAND_Gate
  nand K3 (K3_out, nZ1_nX_out, Z2_nX_out);
  nand J2 (J2_out, Z1_nX_out, Z3_nX_out);
  not nand_2 (Y, Z1_Z2_X_out);  // NAND_Gate
  J_K_Flip_Flop j_k_ff_1 (
    .J(J1_out), .clk(CLK_out), .K(K1_out), .Q(j_k_ff_1_q), .Qn(j_k_ff_1_qn), .reset(Res));  // open: preset, en
  J_K_Flip_Flop j_k_ff_2 (
    .J(J2_out), .clk(CLK_out), .K(1'b1), .Q(j_k_ff_2_q), .Qn(j_k_ff_2_qn), .reset(Res));  // open: preset, en
  J_K_Flip_Flop j_k_ff_3 (
    .J(J3_out), .clk(CLK_out), .K(K3_out), .Q(j_k_ff_3_q), .Qn(j_k_ff_3_qn), .reset(Res));  // open: preset, en
endmodule
